// Logisim project ArithmeticLogicUnitPrototypeProgram.circ as structural Verilog: 2 circuits, main circuit main
module main (
  input  Add_or_Sub_Command,
  input  [3:0] L_Input,
  input  [3:0] R_Input,
  output [3:0] Result,
  output Overflow,
  output Zero,
  output Negative
);

  wire and_6_out, Clk_out, helper_circuit_1_bottom, helper_circuit_1_result, helper_circuit_2_bottom,
       helper_circuit_2_result, helper_circuit_3_bottom, helper_circuit_3_result, helper_circuit_4_bottom,
       helper_circuit_4_result, not_1_out, not_2_out, not_3_out, not_4_out, xor_1_out, xor_2_out, xor_3_out,
       xor_4_out, xor_5_out;

  xor xor_1 (xor_1_out, Add_or_Sub_Command, R_Input[0]);
  xor xor_2 (xor_2_out, Add_or_Sub_Command, R_Input[1]);
  xor xor_3 (xor_3_out, Add_or_Sub_Command, R_Input[2]);
  xor xor_4 (xor_4_out, Add_or_Sub_Command, R_Input[3]);
  Helper_Circuit helper_circuit_1 (
    .input1(L_Input[0]), .input2(xor_1_out), .top(Add_or_Sub_Command), .bottom(helper_circuit_1_bottom),
    .result(helper_circuit_1_result));
  Helper_Circuit helper_circuit_2 (
    .input1(L_Input[1]), .input2(xor_2_out), .top(helper_circuit_1_bottom), .bottom(helper_circuit_2_bottom),
    .result(helper_circuit_2_result));
  Helper_Circuit helper_circuit_3 (
    .input1(L_Input[2]), .input2(xor_3_out), .top(helper_circuit_2_bottom), .bottom(helper_circuit_3_bottom),
    .result(helper_circuit_3_result));
  Helper_Circuit helper_circuit_4 (
    .input1(L_Input[3]), .input2(xor_4_out), .top(helper_circuit_3_bottom), .bottom(helper_circuit_4_bottom),
    .result(helper_circuit_4_result));
  Clock Clk (.out(Clk_out));
  and and_1 (Result[0], Clk_out, helper_circuit_1_result);
  and and_2 (Result[1], Clk_out, helper_circuit_2_result);
  and and_3 (Result[2], Clk_out, helper_circuit_3_result);
  and and_4 (Result[3], Clk_out, helper_circuit_4_result);
  Hex_Digit_Display hex_digit_display_1 (.value(Result));  // open: dp
  not not_1 (not_1_out, Result[0]);
  not not_2 (not_2_out, Result[1]);
  not not_3 (not_3_out, Result[2]);
  not not_4 (not_4_out, Result[3]);
  and and_5 (Negative, Clk_out, Result[3]);
  and and_6 (and_6_out, not_1_out, not_2_out, not_3_out, not_4_out);
  and and_7 (Zero, Clk_out, and_6_out);
  xor xor_5 (xor_5_out, helper_circuit_3_bottom, helper_circuit_4_bottom);
  and and_8 (Overflow, Clk_out, xor_5_out);

  // Notes on the sheet:
  //   Arithmetic Logic Unit Prototype Program
  //   Mohamed Yasser Anwar Mahmoud AlKayd
endmodule

module Helper_Circuit (
  input  top,
  input  input1,
  input  input2,
  output result,
  output bottom
);

  wire and_1_out, and_2_out, xor_1_out;

  xor xor_1 (xor_1_out, input1, input2);
  xor xor_2 (result, xor_1_out, top);
  and and_1 (and_1_out, top, xor_1_out);
  and and_2 (and_2_out, input2, input1);
  or or_1 (bottom, and_1_out, and_2_out);
endmodule
